// Digital circuit mips32soc2.dig as structural Verilog
module mips32soc2 (
  input  clk,
  input  reset,
  input  [7:0] btns_state,
  output [2:0] red,
  output [2:0] green,
  output [1:0] blue,
  output hsync,
  output vsync,
  output invPC,
  output invOp,
  output invAddr,
  output err
);

  wire ALU_Z, aluop, beq, bgez, bgtz, blez, bltz, bne, BR_BT, cclk, en_DM, en_IO, en_VGA, iclk, IM_EN, jal,
       jmp, jr, mbe, mds, memr, msC, multiplexer_2_out, mw, oD, owe, rd1sel, regw, vclk, zE;
  wire [0:0] or_3_out;
  wire [1:0] asrc, m2r, mB, ofs, regdst;
  wire [4:0] bgbl, multiplexer_3_out;
  wire [5:0] Funct;
  wire [10:0] addr;
  wire [12:0] mips32_1_p2;
  wire [27:0] pc_plus_4;
  wire [31:0] add_2_s, ALU_R, inD_DD, IO_OD, multiplexer_4_out, multiplexer_5_out, multiplexer_6_out, oD_RD,
       pc, pc_in, pc_out, rd1, rd2, rd_DM, rd_VGA, sE_OUT, wd;
  wire [31:6] inst;
  wire [31:28] jp_tg;

  Add #(.Bits(32)) add_1 (.a(pc), .b(32'h4), .c_i(1'b0), .s({jp_tg, pc_plus_4}));  // open: c_o
  // mips32 mips32_1: pin names not known; wires that end beside it: pc_out, mips32_1_p2, invPC
  // mips32 mips32_2: pin names not known; wires that end beside it: cclk, reset, msC
  // mips32 mips32_3: pin names not known; wires that end beside it: clk, cclk, vclk, iclk
  or or_1 (err, invPC, invOp, invAddr);
  Multiplexer #(.Bits(32)) multiplexer_1 (.sel(reset), .in_0(pc_in), .in_1(32'h400000), .out(pc_out));
  Multiplexer multiplexer_2 (.sel(err), .in_0(1'b1), .in_1(1'b0), .out(multiplexer_2_out));
  or or_2 (IM_EN, reset, multiplexer_2_out);
  // mips32 #(.AddrBits(11)) mips32_4: pin names not known; wires that end beside it: iclk, IM_EN, mips32_1_p2[12:2], {inst[31:21], bgbl, inst[15:6], Funct}
  Register #(.Bits(32)) register_1 (.D(pc_out), .C(iclk), .en(1'b1), .Q(pc));
  PullDown #(.Bits(32)) pulldown_1 (.out({inst[31:21], bgbl, inst[15:6], Funct}));
  // mips32 mips32_5: pin names not known; wires that end beside it: inst[31:26], Funct, bgbl, jmp, beq, bne, memr, m2r, mw, asrc, rd1sel, regw, regdst, aluop, zE, invOp, mds, mbe, bgez, bgtz, blez, bltz, jr, jal
  // mips32 mips32_6: pin names not known; wires that end beside it: {inst[15:6], Funct}, zE, sE_OUT
  Multiplexer #(.Selector_Bits(2), .Bits(5)) multiplexer_3 (
    .sel(regdst), .in_0(bgbl), .in_1(inst[15:11]), .in_2({5{1'b1}}), .in_3({5{1'b0}}), .out(multiplexer_3_out));
  // mips32 #(.AddrBits(5)) mips32_7: pin names not known; wires that end beside it: inst[25:21], bgbl, multiplexer_3_out, wd, regw, iclk, rd1, rd2
  Multiplexer #(.Bits(32)) multiplexer_4 (.sel(rd1sel), .in_0(rd1), .in_1(rd2), .out(multiplexer_4_out));
  Multiplexer #(.Selector_Bits(2), .Bits(32)) multiplexer_5 (
    .sel(asrc), .in_0(rd2), .in_1(sE_OUT), .in_2(rd1), .in_3({{27{1'b0}}, inst[10:6]}),
    .out(multiplexer_5_out));
  Add #(.Bits(32)) add_2 (.a({jp_tg, pc_plus_4}), .b({sE_OUT[29:0], 2'b00}), .c_i(1'b0), .s(add_2_s));  // open: c_o
  // mips32 mips32_8: pin names not known; wires that end beside it: beq, bne, bgez, bgtz, blez, bltz, ALU_Z, ALU_R[31], BR_BT
  // mips32 mips32_9: pin names not known; wires that end beside it: multiplexer_4_out, multiplexer_5_out, aluop, ALU_R, ALU_Z
  Multiplexer #(.Bits(32)) multiplexer_6 (
    .sel(BR_BT), .in_0({jp_tg, pc_plus_4}), .in_1(add_2_s), .out(multiplexer_6_out));
  or or_3 (or_3_out[0], jmp, jal);
  // mips32 mips32_10: pin names not known; wires that end beside it: ALU_R, mw, memr, {addr, ofs}, {en_IO, en_VGA, en_DM}, mB, invAddr
  Multiplexer #(.Selector_Bits(2), .Bits(32)) multiplexer_7 (
    .sel({jr, or_3_out[0]}), .in_0(multiplexer_6_out),
    .in_1({jp_tg, inst[25:21], bgbl, inst[15:6], Funct, 2'b00}), .in_2(rd1), .in_3({32{1'b0}}), .out(pc_in));
  Multiplexer #(.Selector_Bits(2), .Bits(32)) multiplexer_8 (
    .sel(m2r), .in_0(ALU_R), .in_1(oD_RD), .in_2({inst[15:6], Funct, {16{1'b0}}}), .in_3({jp_tg, pc_plus_4}),
    .out(wd));
  // mips32 mips32_11: pin names not known; wires that end beside it: inD_DD, ofs, mbe, mds, oD_RD
  // mips32 mips32_12: pin names not known; wires that end beside it: rd2, ofs, mw, mds, oD, owe
  // mips32 #(.AddrBits(12)) mips32_13: pin names not known; wires that end beside it: vclk, cclk, reset, en_VGA, owe, addr, oD, rd_VGA, red, green, blue, hsync, vsync
  // mips32 #(.AddrBits(11)) mips32_14: pin names not known; wires that end beside it: cclk, en_DM, owe, addr, oD, rd_DM
  // mips32 mips32_15: pin names not known; wires that end beside it: addr, msC, btns_state, en_IO, IO_OD
  Multiplexer #(.Selector_Bits(2), .Bits(32)) multiplexer_9 (
    .sel(mB), .in_0(rd_DM), .in_1(rd_VGA), .in_2(IO_OD), .in_3({32{1'b0}}), .out(inD_DD));

  // Other names for the same wires on the sheet: addr_DM[10:0] = addr; addr_IO[10:0] = addr; addr_VGA[10:0] = addr;
  //   sign = ALU_R[31]; b[1:0] = blue; btn[7:0] = btns_state; g[2:0] = green; halt = err; hs = hsync; iAd = invAddr;
  //   inst (some bits) = {bgbl, Funct}; jp_tg[27:2] = {inst[25:21], bgbl, inst[15:6], Funct};
  //   LUI[31:16] = {inst[15:6], Funct}; sa[4:0] = inst[10:6]; sa_32[4:0] = inst[10:6]; Opcode[5:0] = inst[31:26];
  //   iOp = invOp; iPC = invPC; mE[2:0] = {en_IO, en_VGA, en_DM}; pc_plus_4[31:28] = jp_tg; r[2:0] = red; rst = reset;
  //   vs = vsync

  // Notes on the sheet:
  //   clk: pin V10, Hz: 100000
  //   reset: pin F17
  //   btns_state: pin M18,L18,M16,L17,K17,K18,C17,C18
  //   red: pin A9,B9,C9
  //   green: pin C10,A10,C11
  //   blue: pin B11,A11
  //   hsync: pin B12
  //   vsync: pin A12
  //   invPC: pin P15
  //   invOp: pin P16
  //   invAddr: pin N15
  //   err: pin N16
  //   contents of mips32_4 (hex, n*v repeats v):
  //   3c1d7fff,37bdfffc,c100021,8100003,41080,442021,42140,3c020001,822021,2402cf00,a22825,
  //   a485b802,3e00008,41080,442021,42100,852021,42040,3405b800,a42021,2403cf00,3405cac0,
  //   80c20000,14400001,3e00008,431025,85382b,3042ffff,24c60001,10e0fffa,24840002,a482fffe,
  //   1000fff5,27bdffd8,3402b800,24043020,afbf0024,afb10020,afb0001c,3403cac0,a4440000,
  //   24420002,1443fffd,3402b800,2403c20a,3404b8a0,a4430000,a4431220,24420002,1444fffc,
  //   3402b800,2403c20a,3404ca20,a4430000,a443009e,244200a0,1444fffc,3c0b1001,25660000,
  //   2405001e,2404000f,c10000d,3c02ffff,3c0f1001,8c590008,7025,afa00010,afa00014,2409001e,
  //   2408000f,25ef0014,256b0000,2410004e,3c03ffff,906d0004,8c620008,31ad00ff,591023,2c4203e9,
  //   14400002,8c790008,25ce0001,31c2000f,304300ff,2c42000a,24650057,10400001,24650030,
  //   24040001,c100004,31a2000f,2c43000a,24450057,10600001,24450030,24040002,c100004,27ac0010,
  //   5025,24180001,14d1006,30420001,91830000,305100ff,10710010,1040000e,1e03025,1202825,
  //   1002025,c10000d,11580016,1140000e,24020002,1142001b,24020003,1142001d,1603025,1202825,
  //   1002025,c10000d,a1910000,254a0001,24020008,258c0001,1542ffe7,1000ffcb,15380004,11090014,
  //   2508ffff,2409004e,1000fff1,2529ffff,1000ffef,15300005,24020026,1102000f,25080001,
  //   24090001,1000ffe9,25290001,1000ffe7,2402001c,11020009,25080001,1000ffe3,11180003,
  //   2508ffff,1000ffe0,2409004e,2408001c,1000ffdd,24090001,24080001,1000ffda
  //   mips32_7 loads RegFile.hex
  //   contents of mips32_13 (hex, n*v repeats v):
  //   0,0,fe,c6,c6,c6,c6,c6,c6,c6,c6,fe,0,0,0,0,0,0,7c,82,aa,82,82,ba,92,82,82,7c,0,0,0,
  //   0,0,0,7c,fe,d6,fe,fe,c6,ee,fe,fe,7c,0,0,0,0,0,0,0,0,6c,fe,fe,fe,fe,7c,38,10,0,0,0,
  //   0,0,0,0,0,18,3c,7e,ff,7e,3c,18,0,0,0,0,0,0,0,18,3c,3c,18,5a,ff,ff,5a,18,3c,0,0,0,
  //   0,0,0,18,18,3c,7e,ff,ff,7e,18,18,3c,0,0,0,0,0,0,0,0,0,0,18,3c,3c,18,0,0,0,0,0,0,ff,
  //   ff,ff,ff,ff,ff,e7,c3,c3,e7,ff,ff,ff,ff,ff,ff,0,0,0,0,0,3c,66,42,42,66,3c,0,0,0,0,
  //   0,ff,ff,ff,ff,ff,c3,99,bd,bd,99,c3,ff,ff,ff,ff,ff,0,0,3e,e,1a,32,78,cc,cc,cc,cc,78,
  //   0,0,0,0,0,0,3c,66,66,66,66,3c,18,7e,18,18,0,0,0,0,0,0,7e,66,7e,60,60,60,60,60,e0,
  //   c0,0,0,0,0,0,0,7e,66,7e,66,66,66,66,66,6e,ec,c0,0,0,0,0,0,0,18,db,7e,3c,e7,3c,7e,
  //   db,18,0,0,0,0,0,0,0,0,c0,f0,fc,ff,ff,fc,f0,c0,0,0,0,0,0,0,0,0,3,f,3f,ff,ff,3f,f,3,
  //   0,0,0,0,0,0,18,3c,7e,18,18,18,18,7e,3c,18,0,0,0,0,0,0,66,66,66,66,66,66,66,0,66,66,
  //   0,0,0,0,0,0,7e,d6,d6,d6,d6,76,16,16,16,16,0,0,0,0,0,3c,66,60,38,6c,66,66,36,1c,6,
  //   66,3c,0,0,0,0,0,0,0,0,0,0,0,fe,fe,fe,fe,0,0,0,0,0,0,18,3c,7e,18,18,18,7e,3c,18,7e,
  //   0,0,0,0,0,0,18,3c,7e,18,18,18,18,18,18,18,0,0,0,0,0,0,18,18,18,18,18,18,18,7e,3c,
  //   18,0,0,0,0,0,0,0,0,0,8,c,fe,fe,c,8,0,0,0,0,0,0,0,0,0,0,20,60,fe,fe,60,20,0,0,0,0,
  //   0,0,0,0,0,c0,c0,c0,c0,c0,fe,0,0,0,0,0,0,0,0,0,0,0,24,66,ff,ff,66,24,0,0,0,0,0,0,0,
  //   0,0,18,18,3c,3c,7e,7e,ff,ff,0,0,0,0,0,0,0,0,ff,ff,7e,7e,3c,3c,18,18,0,0,0,0,0,0,0,
  //   0,0,0,0,0,0,0,0,0,0,0,0,0,0,0,18,18,18,18,18,18,18,0,18,18,0,0,0,0,0,66,66,66,0,0,
  //   0,0,0,0,0,0,0,0,0,0,0,0,6c,6c,6c,fe,6c,6c,fe,6c,6c,6c,0,0,0,0,0,10,10,7c,d6,d0,d0,
  //   7c,16,16,d6,7c,10,10,0,0,0,0,66,d6,6c,c,18,18,30,36,6b,66,0,0,0,0,0,0,38,6c,6c,38,
  //   76,dc,cc,cc,dc,76,0,0,0,0,0,18,18,18,0,0,0,0,0,0,0,0,0,0,0,0,0,0,c,18,30,30,30,30,
  //   30,30,18,c,0,0,0,0,0,0,30,18,c,c,c,c,c,c,18,30,0,0,0,0,0,0,0,0,0,6c,38,fe,38,6c,0,
  //   0,0,0,0,0,0,0,0,0,0,18,18,7e,18,18,0,0,0,0,0,0,0,0,0,0,0,0,0,0,0,0,18,18,30,0,0,0,
  //   0,0,0,0,0,0,0,fe,0,0,0,0,0,0,0,0,0,0,0,0,0,0,0,0,0,0,18,18,0,0,0,0,0,0,6,6,c,c,18,
  //   18,30,30,60,60,0,0,0,0,0,0,7c,c6,c6,ce,de,f6,e6,c6,c6,7c,0,0,0,0,0,0,18,38,78,18,
  //   18,18,18,18,18,7e,0,0,0,0,0,0,7c,c6,c6,6,c,18,30,60,c0,fe,0,0,0,0,0,0,7c,c6,c6,6,
  //   3c,6,6,c6,c6,7c,0,0,0,0,0,0,6,e,1e,36,66,c6,fe,6,6,6,0,0,0,0,0,0,fe,c0,c0,c0,fc,6,
  //   6,6,c6,7c,0,0,0,0,0,0,3c,60,c0,c0,fc,c6,c6,c6,c6,7c,0,0,0,0,0,0,fe,6,6,c,c,18,18,
  //   30,30,30,0,0,0,0,0,0,7c,c6,c6,c6,7c,c6,c6,c6,c6,7c,0,0,0,0,0,0,7c,c6,c6,c6,c6,7e,
  //   6,6,c,78,0,0,0,0,0,0,0,0,0,18,18,0,0,0,18,18,0,0,0,0,0,0,0,0,0,18,18,0,0,0,18,18,
  //   30,0,0,0,0,0,0,6,c,18,30,60,30,18,c,6,0,0,0,0,0,0,0,0,0,fe,0,0,fe,0,0,0,0,0,0,0,0,
  //   0,0,60,30,18,c,6,c,18,30,60,0,0,0,0,0,0,7c,c6,c6,c6,c,18,18,0,18,18,0,0,0,0,0,0,7c,
  //   c6,ce,d6,d6,d6,d6,ce,c0,7e,0,0,0,0,0,0,7c,c6,c6,c6,c6,fe,c6,c6,c6,c6,0,0,0,0,0,0,
  //   fc,c6,c6,c6,fc,c6,c6,c6,c6,fc,0,0,0,0,0,0,7c,c6,c6,c0,c0,c0,c0,c6,c6,7c,0,0,0,0,0,
  //   0,f8,cc,c6,c6,c6,c6,c6,c6,cc,f8,0,0,0,0,0,0,fe,c0,c0,c0,f8,c0,c0,c0,c0,fe,0,0,0,0,
  //   0,0,fe,c0,c0,c0,f8,c0,c0,c0,c0,c0,0,0,0,0,0,0,7c,c6,c6,c0,c0,de,c6,c6,c6,7c,0,0,0,
  //   0,0,0,c6,c6,c6,c6,fe,c6,c6,c6,c6,c6,0,0,0,0,0,0,3c,18,18,18,18,18,18,18,18,3c,0,0,
  //   0,0,0,0,1e,c,c,c,c,c,c,cc,cc,78,0,0,0,0,0,0,c6,c6,cc,d8,f0,f0,d8,cc,c6,c6,0,0,0,0,
  //   0,0,c0,c0,c0,c0,c0,c0,c0,c0,c0,fe,0,0,0,0,0,0,82,c6,ee,fe,d6,c6,c6,c6,c6,c6,0,0,0,
  //   0,0,0,c6,c6,c6,e6,f6,de,ce,c6,c6,c6,0,0,0,0,0,0,7c,c6,c6,c6,c6,c6,c6,c6,c6,7c,0,0,
  //   0,0,0,0,fc,c6,c6,c6,c6,fc,c0,c0,c0,c0,0,0,0,0,0,0,7c,c6,c6,c6,c6,c6,c6,c6,de,7c,6,
  //   0,0,0,0,0,fc,c6,c6,c6,c6,fc,f0,d8,cc,c6,0,0,0,0,0,0,7c,c6,c0,c0,7c,6,6,c6,c6,7c,0,
  //   0,0,0,0,0,ff,18,18,18,18,18,18,18,18,18,0,0,0,0,0,0,c6,c6,c6,c6,c6,c6,c6,c6,c6,7c,
  //   0,0,0,0,0,0,c6,c6,c6,c6,c6,6c,6c,6c,38,38,0,0,0,0,0,0,c6,c6,c6,c6,c6,d6,fe,ee,c6,
  //   82,0,0,0,0,0,0,c6,c6,6c,6c,38,38,6c,6c,c6,c6,0,0,0,0,0,0,c3,c3,66,66,3c,18,18,18,
  //   18,18,0,0,0,0,0,0,fe,6,6,c,18,30,60,c0,c0,fe,0,0,0,0,0,0,3c,30,30,30,30,30,30,30,
  //   30,3c,0,0,0,0,0,0,60,60,30,30,18,18,c,c,6,6,0,0,0,0,0,0,3c,c,c,c,c,c,c,c,c,3c,0,0,
  //   0,0,0,18,3c,66,0,0,0,0,0,0,0,0,0,0,0,0,0,0,0,0,0,0,0,0,0,0,0,0,0,fe,0,0,30,18,0,0,
  //   0,0,0,0,0,0,0,0,0,0,0,0,0,0,0,0,0,7c,6,7e,c6,c6,c6,7e,0,0,0,0,0,0,c0,c0,c0,fc,c6,
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  //   contents of mips32_14 (hex, n*v repeats v):
  //   48656c6c,6f20576f,726c6420,46726f6d,20432100,20202020,20202020,20202020,20202020,
  //   20202000
endmodule
